# Fritzing sketch Harald (saved by Fritzing 0.9.9b)
breadboards: 1

parts:
  LED1 = LED - 5mm [color="Red (633nm)" current=0.030 package="5 mm [THT]"]
  Mod1 = Raspberry Pi 4B  # not connected
  J1 = Raspberry Pi Header 40pin [package=THT]
  LED2 = LED - 5mm [color="Green (555nm)" current=0.030 package="5 mm [THT]"]
  R2 = Resistor [tolerance=±5% power=0.25 resistance=10k package=THT]
  R3 = Resistor [tolerance=±5% power=0.25 resistance=10k package=THT]
  R4 = Resistor [tolerance=±5% power=0.25 resistance=10 package=THT]
  R5 = Resistor [tolerance=±5% power=0.25 resistance=150 package=THT]
  Part1 = RFID-RC522-v2
  OLED1 = OLED 128x64 I2C Monochrome Display GND-VDD

nets:
  GND: LED1.cathode, J1.GND, LED2.cathode, Part1.GND, OLED1.GND
  N1: LED1.anode, R5.Pin_1
  3V3: J1.3V3, R2.Pin_0, R3.Pin_0, Part1.3.3V, OLED1.VDD
  N2: J1.GPIO2, R2.Pin_1, OLED1.SDA
  N3: J1.IO3, R3.Pin_1, OLED1.SCK
  N4: J1.IO23, R5.Pin_0
  N5: J1.IO24, R4.Pin_0
  N6: J1.IO10, Part1.MOSI
  N7: J1.IO9, Part1.MISO
  N8: J1.IO25, Part1.RST
  N9: J1.IO11, Part1.SCK
  N10: J1.IO8, Part1.SDA
  N11: LED2.anode, R4.Pin_1

custom parts:
  Raspberry Pi Header 40pin: Raspberry Pi 40 pin header - for creating your own shields. (Mar 2020, bb: make breadboard friendly (.4in pin spacing) and add labels. Schematic add labels. PCB make oblong pins to allow routing traces between the pins.)
  RFID-RC522-v2: A simple China made RFID-RC522 Reader; do check the pin labels, as this is a MFRC522 based clone.
  OLED 128x64 I2C Monochrome Display GND-VDD: OLED 128x64 I2C Monochrome Display. Note: there are two variants of this part, this one is the GND VDD SCK SDA variant. The other is VDD GND SCK SDA. Make sure you select the part that matches your module as using the incorrect part will probably destroy your module! In addition the mounting holes are marked on silkscreen but not by default drilled. If you want drilled mounting holes, copy a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
