# Fritzing sketch Harald2 (saved by Fritzing 0.9.9b)

parts:
  LED1 = LED - 5mm [color="Red (633nm)" current=0.030 package="5 mm [THT]"]
  RPi_4 = Raspberry Pi 4B
  LED2 = LED - 5mm [color="Green (555nm)" current=0.030 package="5 mm [THT]"]
  R2 = Resistor [tolerance=±5% power=0.25 resistance=10 package=THT]
  R1 = Resistor [tolerance=±5% power=0.25 resistance=150 package=THT]
  RC522 = RFID-RC522-v2
  OLED1 = OLED 128x64 I2C Monochrome Display GND-VDD

nets:
  N1: LED1.cathode, LED2.cathode
  N2: LED1.anode, R1.Pin_1
  3V3: RPi_4.3V3, RC522.3.3V, OLED1.VDD
  N3: RPi_4.GPIO2, OLED1.SDA
  N4: RPi_4.GPIO3, OLED1.SCK
  GND: RPi_4.GND, OLED1.GND
  N5: RPi_4.GPIO23, R1.Pin_0
  N6: RPi_4.GPIO24, R2.Pin_0
  N7: RPi_4.GPIO10, RC522.MOSI
  N8: RPi_4.GPIO9, RC522.MISO
  N9: RPi_4.GPIO25, RC522.GND
  N10: RPi_4.GPIO11, RC522.SCK
  N11: RPi_4.GPIO8, RC522.SDA
  N12: LED2.anode, R2.Pin_1

custom parts:
  RFID-RC522-v2: A simple China made RFID-RC522 Reader; do check the pin labels, as this is a MFRC522 based clone.
  OLED 128x64 I2C Monochrome Display GND-VDD: OLED 128x64 I2C Monochrome Display. Note: there are two variants of this part, this one is the GND VDD SCK SDA variant. The other is VDD GND SCK SDA. Make sure you select the part that matches your module as using the incorrect part will probably destroy your module! In addition the mounting holes are marked on silkscreen but not by default drilled. If you want drilled mounting holes, copy a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
